# Fritzing sketch ventilastation-esp32s3 (saved by Fritzing 0.9.4)
perfboards: 3

parts:
  J30 = double row male pin header, 4 pins [form="♂ (male)"]
  Q4 = NPN-Transistor [package="TO92 [THT]"]
  J31 = male pin header, 3 pins [form="♂ (male)"]
  M1 = MAX485 Breakout [package=THT]
  DOTSTAR1 = DotStar Strip -- Black (60/m) [part_number=2239]
  J33 = screw terminal, 3 pins
  J34 = screw terminal, 3 pins
  C1 = Electrolytic Capacitor [capacitance=100µF voltage=16V package="200 mil [THT, electrolytic]"]
  R1 = Resistor [tolerance=±5% resistance=4.7k package=THT]
  R2 = Resistor [tolerance=±5% resistance=10k package=THT]
  R3 = Resistor [tolerance=±5% resistance=1k package=THT]
  M2 = MAX485 Breakout [package=THT]
  A1 = Werner Rothschopf (modified to ESP32-S3-DevKitC dual USB by vanepp Aug 2024)
  M3 = MAX485 Breakout [package=THT]
  M4 = MAX485 Breakout [package=THT]
  Raspberry_Pi_1 = Raspberry Pi 3 [part_number=RPI-3-V1.2]
  J35 = screw terminal, 6 pins
  J38 = ATX24 Pin Power Supply Connector [package=atx24_right_angle]
  J39 = screw terminal, 4 pins
  J40 = screw terminal, 6 pins
  S1 = Taiway 100-SP-X-T1 SPDT Miniature Toggle Switch [part_number=100-SP-X-T1-0-0-B1-M1 package=THT]
  R4 = Resistor [tolerance=±5% resistance=10k package=THT]
  R5 = Resistor [tolerance=±5% resistance=4.7k package=THT]

nets:
  N1: J30.pin1, Q4.E, J31.pin3, DOTSTAR1.+5V, C1.+
  N2: J30.pin2, DOTSTAR1.CI, A1.Pin_8
  N3: J30.pin3, DOTSTAR1.DI, A1.Pin_9
  GND: J30.pin4, Q4.C, J31.pin2, M1.GND, DOTSTAR1.GND, J33.pin3, C1.-, R2.Pin_1, M2.RE, M2.DE, M2.GND, A1.Pin_22, A1.Pin_23, A1.Pin_24, A1.Pin_44, M3.GND, M4.GND, Raspberry_Pi_1.GND, J35.pin3, J38.GND, J39.pin1, J40.pin3, S1.L1
  N4: Q4.B, J31.pin1, R3.Pin_1, A1.Pin_4
  VCC: M1.RE, M1.DE, M1.VCC, J34.pin1, M2.VCC, A1.Pin_21, Raspberry_Pi_1.5V, J35.pin4, J38.5V, J39.pin4, J40.pin4
  N5: M1.DI, J33.pin1, A1.Pin_16, J39.pin2
  N6: M1.A, M1.A1, M3.A, M3.A1, J35.pin1, J40.pin1
  N7: M1.B, J35.pin2, J40.pin2
  N8: J34.pin3, R1.Pin_0, M2.RO, J39.pin3
  N9: R2.Pin_0, A1.Pin_15
  N10: R3.Pin_0, A1.Pin_1, A1.Pin_2
  N11: M2.A, M2.A1, J35.pin5, J40.pin5
  N12: M2.B, M4.B, J35.pin6, J40.pin6
  N13: M3.RO, R5.Pin_0
  N14: M3.RE, M3.DE, R4.Pin_1
  VCC_2: M3.VCC, M4.RE, M4.DE, M4.VCC, Raspberry_Pi_1.3V3
  N15: M4.A, M4.A1
  N16: J38.PS_ON, S1.COM

notes:
  A3144 - hall sensor
  107 x APA102 - (144led/m, ipx65)
  1000µF - 16V
  1kΩ
  10kΩ
  4k7
  ESP32 S3 N16R8
  2 x MAX485
  FALTA CORREGIR
  En un extremo de la paleta
  Fuente ATX
  Interruptor
  Raspberry PI (2 o superior)
  5V DC
  3.3V DC
  ESP32-CAM-MB

custom parts:
  MAX485 Breakout: MAX485 RS485 breakout board
  DotStar Strip -- Black (60/m): NeopixelDotStar Strip, Black, 60 pixels per meter.
  Werner Rothschopf (modified to ESP32-S3-DevKitC dual USB by vanepp Aug 2024): ESP32-S3 ESP32-S3-DevKitC-1 Dual USB development board Pyboard CircuitPython Micropython wifi BLE5.0 ESP32-S3.
