# Fritzing sketch pre-voom (saved by Fritzing 0.9.4)
breadboards: 2

parts:
  LCD1 = 2.8" SPI TFT Module [part_number=MSP2807]
  A1 = Werner Rothschopf (modified to ESP32-S3-DevKitC dual USB by vanepp Aug 2024)
  U1 = SD_CARD_SOCKET [package=sdcard_4uconn]
  Part1 = Thumb Joystick
  Menu = Momentary Switch [package=ksa_sealed_tac_switch]
  Option = Momentary Switch [package=ksa_sealed_tac_switch]
  Start = Momentary Switch [package=ksa_sealed_tac_switch]
  A = Momentary Switch [package=ksa_sealed_tac_switch]
  Select = Momentary Switch [package=ksa_sealed_tac_switch]
  Power_5v_DC = Power plug

nets:
  N1: LCD1.pin1, LCD1.pin8, A1.Pin_21, Power_5v_DC.VCC
  GND: LCD1.pin2, A1.Pin_22, A1.Pin_23, A1.Pin_24, A1.Pin_44, U1.VSS1, U1.VSS2, Part1.GND, Menu.4, Option.4, Start.4, A.4, Select.4, Power_5v_DC.GND
  N2: LCD1.pin3, A1.Pin_12
  N3: LCD1.pin4, A1.Pin_5
  N4: LCD1.pin5, A1.Pin_8
  N5: LCD1.pin6, A1.Pin_11
  N6: LCD1.pin7, A1.Pin_9
  N7: LCD1.pin9, A1.Pin_10
  VDD: A1.Pin_1, A1.Pin_2, U1.VDD, Part1.VCC
  N8: A1.Pin_6, Part1.VERT
  N9: A1.Pin_7, Part1.HORZ
  N10: A1.Pin_17, U1.CMD
  N11: A1.Pin_18, U1.CLK
  N12: A1.Pin_19, U1.DAT0
  N13: A1.Pin_20, U1.CD_DAT3
  N14: A1.Pin_35, Select.2
  N15: A1.Pin_36, Start.2
  N16: A1.Pin_37, Menu.2
  N17: A1.Pin_38, Option.2
  N18: A1.Pin_39, A.2
  N19: A1.Pin_40, Part1.SEL

notes:
  5v DC
  3.3v
  5v

custom parts:
  2.8" SPI TFT Module: A generic 2.8 inch LCD TFT 320x240 display with touchscreen and SD card slot. Uses the ILI9341 controller, like the Adafruit displays of this size uses.
  Werner Rothschopf (modified to ESP32-S3-DevKitC dual USB by vanepp Aug 2024): ESP32-S3 ESP32-S3-DevKitC-1 Dual USB development board Pyboard CircuitPython Micropython wifi BLE5.0 ESP32-S3.
